# Fritzing sketch paddle-adapter (saved by Fritzing 1.0.4)
breadboards: 1

parts:
  R1 = Resistor [tolerance=±5% power=0.25W resistance=2.2k package=THT]
  R2 = Resistor [tolerance=±5% power=0.25W resistance=2.2k package=THT]
  X2 = DB9 Connector [package=db9]
  Part1 = Arduino Uno (Rev3)

nets:
  N1: R1.Pin_0, X2.5
  N2: R1.Pin_1, R2.Pin_1, X2.2, Part1.A2, Part1.A3, Part1.GND
  N3: R2.Pin_0, X2.3
  N4: X2.6, Part1.A1
  N5: X2.7, Part1.A0
